// Logisim project Labo4.circ as structural Verilog: 3 circuits, main circuit LatchD
module LatchD (
  input  D,
  input  LD,
  output Q,
  output Q2
);

  wire and_1_out, and_2_out, not_1_out;

  not not_1 (not_1_out, D);
  and and_1 (and_1_out, not_1_out, LD);
  and and_2 (and_2_out, LD, D);
  nor nor_1 (Q, and_1_out, Q2);
  nor nor_2 (Q2, Q, and_2_out);

  // Notes on the sheet:
  //   Attention, votre version de Logisim
  //   ne contient pas de tracker. Si vous
  //   enregistrez votre projet, toutes les
  //   informations du tracker seront
  //   définitivement effacées.
endmodule

module FlipFlop (
  input  D,
  input  CK,
  output Q,
  output Q2
);

  wire Maitre_q, not_1_out, not_2_out;

  not not_1 (not_1_out, CK);
  LatchD Maitre (.D(D), .LD(not_1_out), .Q(Maitre_q));  // open: Q2
  not not_2 (not_2_out, not_1_out);
  LatchD latchd_1 (.D(Maitre_q), .LD(not_2_out), .Q(Q), .Q2(Q2));

  // Notes on the sheet:
  //   Attention, votre version de Logisim
  //   ne contient pas de tracker. Si vous
  //   enregistrez votre projet, toutes les
  //   informations du tracker seront
  //   définitivement effacées.
endmodule

module ShiftRegistre4bits (
  input  D3,
  input  in_2,
  input  in_3,
  input  R,
  input  in_5,
  input  [1:0] S,
  input  [1:0] in_7,
  input  CK,
  input  in_9,
  output out_10,
  output out_11
);

  wire d_ff_2_q, multiplexer_1_out, multiplexer_2_out, multiplexer_3_out;

  Multiplexer #(.select(2), .enable("false")) multiplexer_1 (
    .in0(out_10), .in2(D3), .in3(R), .out(multiplexer_1_out), .sel(S));  // open: in1
  D_Flip_Flop d_ff_1 (.D(multiplexer_1_out), .clk(CK), .Q(out_10));  // open: Qn, preset, reset
  Multiplexer #(.select(2), .enable("false")) multiplexer_2 (
    .in2(in_2), .in3(out_10), .out(multiplexer_2_out));  // open: in0, in1, sel
  D_Flip_Flop d_ff_2 (.D(multiplexer_2_out), .clk(CK), .Q(d_ff_2_q));  // open: Qn, preset, reset
  Multiplexer #(.select(2), .enable("false")) multiplexer_3 (
    .in0(out_11), .in2(in_3), .in3(in_5), .out(multiplexer_3_out), .sel(in_7));  // open: in1
  D_Flip_Flop d_ff_3 (.D(multiplexer_3_out), .clk(in_9), .Q(out_11));  // open: Qn, preset, reset

  // Notes on the sheet:
  //   Attention, votre version de Logisim
  //   ne contient pas de tracker. Si vous
  //   enregistrez votre projet, toutes les
  //   informations du tracker seront
  //   définitivement effacées.
endmodule
