// Logisim project Labo5_UART.circ as structural Verilog: 16 circuits, main circuit LatchD
module LatchD (
  input  D,
  input  LD,
  output Q,
  output Q2
);

  wire and_1_out, and_2_out, not_1_out;

  not not_1 (not_1_out, D);
  and and_1 (and_1_out, not_1_out, LD);
  and and_2 (and_2_out, LD, D);
  nor nor_1 (Q, and_1_out, Q2);
  nor nor_2 (Q2, Q, and_2_out);

  // Notes on the sheet:
  //   Attention, votre version de Logisim
  //   ne contient pas de tracker. Si vous
  //   enregistrez votre projet, toutes les
  //   informations du tracker seront
  //   définitivement effacées.
endmodule

module FlipFlop (
  input  D,
  input  CK,
  output Q,
  output Q2
);

  wire Maitre_q, not_1_out, not_2_out;

  not not_1 (not_1_out, CK);
  LatchD Maitre (.D(D), .LD(not_1_out), .Q(Maitre_q));  // open: Q2
  not not_2 (not_2_out, not_1_out);
  LatchD latchd_1 (.D(Maitre_q), .LD(not_2_out), .Q(Q), .Q2(Q2));

  // Notes on the sheet:
  //   Attention, votre version de Logisim
  //   ne contient pas de tracker. Si vous
  //   enregistrez votre projet, toutes les
  //   informations du tracker seront
  //   définitivement effacées.
endmodule

module ShiftRegistre4bits (
  input  D3,
  input  D2,
  input  D1,
  input  D0,
  input  L,
  input  R,
  input  [1:0] S,
  input  CK,
  output Q3,
  output Q2,
  output Q1,
  output Q0
);

  wire multiplexer_1_out, multiplexer_2_out, multiplexer_3_out, multiplexer_4_out;

  Multiplexer #(.select(2), .enable("false")) multiplexer_1 (
    .in0(Q3), .in1(D3), .in2(Q2), .in3(R), .out(multiplexer_1_out), .sel(S));
  D_Flip_Flop d_ff_1 (.D(multiplexer_1_out), .clk(CK), .Q(Q3));  // open: Qn, preset, reset
  Multiplexer #(.select(2), .enable("false")) multiplexer_2 (
    .in0(Q2), .in1(D2), .in2(Q1), .in3(Q3), .out(multiplexer_2_out), .sel(S));
  D_Flip_Flop d_ff_2 (.D(multiplexer_2_out), .clk(CK), .Q(Q2));  // open: Qn, preset, reset
  Multiplexer #(.select(2), .enable("false")) multiplexer_3 (
    .in0(Q1), .in1(D1), .in2(Q0), .in3(Q2), .out(multiplexer_3_out), .sel(S));
  D_Flip_Flop d_ff_3 (.D(multiplexer_3_out), .clk(CK), .Q(Q1));  // open: Qn, preset, reset
  Multiplexer #(.select(2), .enable("false")) multiplexer_4 (
    .in0(Q0), .in1(D0), .in2(L), .in3(Q1), .out(multiplexer_4_out), .sel(S));
  D_Flip_Flop d_ff_4 (.D(multiplexer_4_out), .clk(CK), .Q(Q0));  // open: Qn, preset, reset

  // Notes on the sheet:
  //   Attention, votre version de Logisim
  //   ne contient pas de tracker. Si vous
  //   enregistrez votre projet, toutes les
  //   informations du tracker seront
  //   définitivement effacées.
endmodule

module ShiftRegistre8bits (
  input  [1:0] S,
  input  L,
  input  R,
  input  [7:0] Inflow,
  output BIT_OUT,
  output [7:0] Outflow
);

  wire CK;

  Clock clock_1 (.out(CK));
  ShiftRegistre4bits SR_1 (
    .D3(Inflow[3]), .D2(Inflow[2]), .D1(Inflow[1]), .D0(Inflow[0]), .L(L), .R(Outflow[4]), .S(S), .CK(CK),
    .Q3(Outflow[3]), .Q2(Outflow[2]), .Q1(Outflow[1]), .Q0(BIT_OUT));
  ShiftRegistre4bits SR_2 (
    .D3(Inflow[7]), .D2(Inflow[6]), .D1(Inflow[5]), .D0(Inflow[4]), .L(Outflow[3]), .R(R), .S(S), .CK(CK),
    .Q3(Outflow[7]), .Q2(Outflow[6]), .Q1(Outflow[5]), .Q0(Outflow[4]));

  assign Outflow[0] = BIT_OUT;

  // Notes on the sheet:
  //   Attention, votre version de Logisim
  //   ne contient pas de tracker. Si vous
  //   enregistrez votre projet, toutes les
  //   informations du tracker seront
  //   définitivement effacées.
endmodule

module LFSR4bits (
  input  in_1,
  input  in_2,
  input  in_3,
  input  in_4,
  input  in_5,
  input  [1:0] in_6,
  input  in_7,
  output out_8,
  output out_9
);

  wire d_ff_3_q, d_ff_4_q, multiplexer_1_out, multiplexer_2_out, multiplexer_3_out, multiplexer_4_out,
       xor_1_out;

  Multiplexer #(.select(2), .enable("false")) multiplexer_1 (
    .in0(out_8), .in1(out_9), .in2(in_1), .in3(xor_1_out), .out(multiplexer_1_out), .sel(in_6));
  D_Flip_Flop d_ff_1 (.D(multiplexer_1_out), .clk(in_7), .Q(out_8));  // open: Qn, preset, reset
  Multiplexer #(.select(2), .enable("false")) multiplexer_2 (
    .in0(out_9), .in1(d_ff_3_q), .in2(in_2), .in3(out_8), .out(multiplexer_2_out), .sel(in_6));
  D_Flip_Flop d_ff_2 (.D(multiplexer_2_out), .clk(in_7), .Q(out_9));  // open: Qn, preset, reset
  Multiplexer #(.select(2), .enable("false")) multiplexer_3 (
    .in0(d_ff_3_q), .in1(d_ff_4_q), .in2(in_3), .in3(out_9), .out(multiplexer_3_out), .sel(in_6));
  xor xor_1 (xor_1_out, d_ff_3_q, d_ff_4_q);
  D_Flip_Flop d_ff_3 (.D(multiplexer_3_out), .clk(in_7), .Q(d_ff_3_q));  // open: Qn, preset, reset
  Multiplexer #(.select(2), .enable("false")) multiplexer_4 (
    .in0(d_ff_4_q), .in1(in_5), .in2(in_4), .in3(d_ff_3_q), .out(multiplexer_4_out), .sel(in_6));
  D_Flip_Flop d_ff_4 (.D(multiplexer_4_out), .clk(in_7), .Q(d_ff_4_q));  // open: Qn, preset, reset

  // Other names for the same wires on the sheet: S[1:0] = in_6

  // Notes on the sheet:
  //   Attention, votre version de Logisim
  //   ne contient pas de tracker. Si vous
  //   enregistrez votre projet, toutes les
  //   informations du tracker seront
  //   définitivement effacées.
endmodule

module Compteur03 (
  input  in_1,
  input  in_2,
  output [1:0] Q,
  output out_4
);

  wire and_1_out, and_2_out, and_3_out, CK, not_1_out, xor_1_out, xor_2_out;

  Clock u_CK (.out(CK));
  not not_1 (not_1_out, in_2);
  xor xor_1 (xor_1_out, Q[0], in_1);
  and and_1 (and_1_out, Q[0], in_1);
  xor xor_2 (xor_2_out, Q[1], and_1_out);
  D_Flip_Flop d_ff_1 (.D(and_2_out), .clk(CK), .Q(Q[0]));  // open: Qn, preset, reset
  and and_2 (and_2_out, xor_1_out, not_1_out);
  D_Flip_Flop d_ff_2 (.D(and_3_out), .clk(CK), .Q(Q[1]));  // open: Qn, preset, reset
  and and_3 (and_3_out, xor_2_out, not_1_out);
  and and_4 (out_4, Q[0], Q[1]);

  // Notes on the sheet:
  //   Attention, votre version de Logisim
  //   ne contient pas de tracker. Si vous
  //   enregistrez votre projet, toutes les
  //   informations du tracker seront
  //   définitivement effacées.
endmodule

module Compteur07 (
  input  en,
  input  Reset,
  output [2:0] Q,
  output Done7
);

  wire and_1_out, and_2_out, and_3_out, and_4_out, and_5_out, CK, not_1_out, xor_1_out, xor_2_out, xor_3_out;

  Clock clock_1 (.out(CK));
  not not_1 (not_1_out, Reset);
  xor xor_1 (xor_1_out, Q[0], en);
  and and_1 (and_1_out, Q[0], en);
  xor xor_2 (xor_2_out, Q[1], and_1_out);
  and and_2 (and_2_out, Q[1], and_1_out);
  xor xor_3 (xor_3_out, Q[2], and_2_out);
  D_Flip_Flop d_ff_1 (.D(and_3_out), .clk(CK), .Q(Q[0]));  // open: Qn, preset, reset
  and and_3 (and_3_out, xor_1_out, not_1_out);
  D_Flip_Flop d_ff_2 (.D(and_4_out), .clk(CK), .Q(Q[1]));  // open: Qn, preset, reset
  and and_4 (and_4_out, xor_2_out, not_1_out);
  D_Flip_Flop d_ff_3 (.D(and_5_out), .clk(CK), .Q(Q[2]));  // open: Qn, preset, reset
  and and_5 (and_5_out, xor_3_out, not_1_out);
  and and_6 (Done7, Q[0], Q[1], Q[2]);

  // Notes on the sheet:
  //   Attention, votre version de Logisim
  //   ne contient pas de tracker. Si vous
  //   enregistrez votre projet, toutes les
  //   informations du tracker seront
  //   définitivement effacées.
endmodule

module CPT3_normal (
  input  count3,
  output [1:0] comptage3,
  output done3
);

  wire and_1_out, and_2_out, CK, not_1_out, xor_1_out;

  Clock clock_1 (.out(CK));
  not not_1 (not_1_out, comptage3[0]);
  and and_1 (and_1_out, not_1_out, count3);
  xor xor_1 (xor_1_out, comptage3[1], comptage3[0]);
  and and_2 (and_2_out, xor_1_out, count3);
  D_Flip_Flop d_ff_1 (.D(and_1_out), .clk(CK), .Q(comptage3[0]));  // open: Qn, preset, reset
  D_Flip_Flop d_ff_2 (.D(and_2_out), .clk(CK), .Q(comptage3[1]));  // open: Qn, preset, reset
  and and_3 (done3, comptage3[0], comptage3[1]);

  // Notes on the sheet:
  //   Attention, votre version de Logisim
  //   ne contient pas de tracker. Si vous
  //   enregistrez votre projet, toutes les
  //   informations du tracker seront
  //   définitivement effacées.
endmodule

module CPT3 (
  input  count3,
  output [1:0] Comptage3,
  output Done3
);

  wire and_1_out, and_2_out, CK, not_1_out, not_2_out, xor_1_out;

  Clock clock_1 (.out(CK));
  not not_1 (not_1_out, Comptage3[0]);
  and and_1 (and_1_out, not_1_out, count3);
  xor xor_1 (xor_1_out, Comptage3[1], Comptage3[0]);
  and and_2 (and_2_out, xor_1_out, count3);
  D_Flip_Flop d_ff_1 (.D(and_1_out), .clk(CK), .Q(Comptage3[0]));  // open: Qn, preset, reset
  D_Flip_Flop d_ff_2 (.D(and_2_out), .clk(CK), .Q(Comptage3[1]));  // open: Qn, preset, reset
  not not_2 (not_2_out, Comptage3[0]);
  and and_3 (Done3, not_2_out, Comptage3[1]);

  // Notes on the sheet:
  //   Attention, votre version de Logisim
  //   ne contient pas de tracker. Si vous
  //   enregistrez votre projet, toutes les
  //   informations du tracker seront
  //   définitivement effacées.
endmodule

module CPT7 (
  input  in_1,
  input  clk,
  output [2:0] out_3,
  output out_4
);

  wire and_1_out, and_2_out, and_3_out, and_4_out, and_5_out, not_1_out, not_2_out, or_1_out, xor_1_out,
       xor_2_out;

  not not_1 (not_1_out, out_3[0]);
  xor xor_1 (xor_1_out, out_3[1], out_3[0]);
  xor xor_2 (xor_2_out, out_3[2], out_3[0]);
  not not_2 (not_2_out, out_3[1]);
  and and_1 (and_1_out, not_2_out, out_3[2]);
  and and_2 (and_2_out, not_1_out, in_1);
  and and_3 (and_3_out, xor_1_out, in_1);
  and and_4 (and_4_out, xor_2_out, out_3[1]);
  D_Flip_Flop d_ff_1 (.D(and_2_out), .clk(clk), .Q(out_3[0]));  // open: Qn, preset, reset
  D_Flip_Flop d_ff_2 (.D(and_3_out), .clk(clk), .Q(out_3[1]));  // open: Qn, preset, reset
  D_Flip_Flop d_ff_3 (.D(and_5_out), .clk(clk), .Q(out_3[2]));  // open: Qn, preset, reset
  or or_1 (or_1_out, and_4_out, and_1_out);
  and and_5 (and_5_out, or_1_out, in_1);
  and and_6 (out_4, out_3[0], out_3[1], out_3[2]);

  // Other names for the same wires on the sheet: CK = clk

  // Notes on the sheet:
  //   Attention, votre version de Logisim
  //   ne contient pas de tracker. Si vous
  //   enregistrez votre projet, toutes les
  //   informations du tracker seront
  //   définitivement effacées.
endmodule

module FSM (
  input  T2,
  input  T1,
  input  T0,
  input  U1,
  input  U0,
  input  V0,
  input  clk,
  output CPT7,
  output CPT3,
  output SEND
);

  wire a, and_1_out, and_2_out, and_3_out, and_4_out, b, c, nand_1_out, nand_2_out, or_1_out, or_2_out,
       or_3_out;

  and and_1 (and_1_out, CPT7, T2, T1, T0);
  or or_1 (or_1_out, ~V0, and_1_out);  // OR_Gate
  D_Flip_Flop d_ff_1 (.D(or_1_out), .clk(clk), .Q(a));  // open: Qn, preset, reset
  and and_2 (and_2_out, V0, a);
  D_Flip_Flop d_ff_2 (.D(and_2_out), .clk(clk), .Q(b));  // open: Qn, preset, reset
  nand nand_1 (nand_1_out, T2, T1, T0);
  and and_3 (and_3_out, nand_1_out, CPT7);
  D_Flip_Flop d_ff_3 (.D(or_2_out), .clk(clk), .Q(c));  // open: Qn, preset, reset
  or or_2 (or_2_out, and_3_out, b);
  nand nand_2 (nand_2_out, U0, U1, CPT3);
  D_Flip_Flop d_ff_4 (.D(or_3_out), .clk(clk), .Q(CPT3));  // open: Qn, preset, reset
  or or_3 (or_3_out, nand_2_out, c);
  D_Flip_Flop d_ff_5 (.D(and_4_out), .clk(clk), .Q(CPT7));  // open: Qn, preset, reset
  and and_4 (and_4_out, U0, U1, CPT3);

  assign SEND = CPT3;

  // Other names for the same wires on the sheet: CK = clk; d = CPT3; e = CPT7

  // Notes on the sheet:
  //   Attention, votre version de Logisim
  //   ne contient pas de tracker. Si vous
  //   enregistrez votre projet, toutes les
  //   informations du tracker seront
  //   définitivement effacées.
endmodule

module CPT7_RS (
  input  in_1,
  output [2:0] out_2,
  output out_3
);

  wire CK, undriven, undriven_2, xor_1_out;

  Clock clock_1 (.out(CK));
  xor xor_1 (xor_1_out, out_2[0], in_1);
  D_Flip_Flop d_ff_1 (.D(xor_1_out), .clk(CK), .Q(out_2[0]));  // open: Qn, preset, reset
  D_Flip_Flop d_ff_2 (.D(undriven), .clk(CK), .Q(out_2[1]));  // open: Qn, preset, reset
  D_Flip_Flop d_ff_3 (.D(undriven_2), .clk(CK), .Q(out_2[2]));  // open: Qn, preset, reset
  and and_1 (out_3, out_2[0], out_2[1], out_2[2]);

  // Notes on the sheet:
  //   Attention, votre version de Logisim
  //   ne contient pas de tracker. Si vous
  //   enregistrez votre projet, toutes les
  //   informations du tracker seront
  //   définitivement effacées.
endmodule

module UART (
  input  in_1,
  output out_2
);

  wire clock_1_out, cpt3_1_p2, cpt3_1_p4, cpt7_1_out_4, fsm_1_cpt7;
  wire [1:0] cpt3_1_p3;
  wire [2:0] cpt7_1_out_3;

  Clock clock_1 (.out(clock_1_out));
  CPT7 cpt7_1 (.in_1(fsm_1_cpt7), .clk(clock_1_out), .out_3(cpt7_1_out_3), .out_4(cpt7_1_out_4));
  // CPT3 cpt3_1: pin names not known; wires that end beside it: clock_1_out, cpt3_1_p2, cpt3_1_p3, cpt3_1_p4
  FSM fsm_1 (
    .T2(cpt7_1_out_3[2]), .T1(cpt7_1_out_3[1]), .T0(cpt7_1_out_3[0]), .U1(cpt3_1_p3[1]), .U0(cpt3_1_p3[0]),
    .V0(in_1), .clk(clock_1_out), .CPT7(fsm_1_cpt7), .CPT3(cpt3_1_p2), .SEND(out_2));

  // Notes on the sheet:
  //   Attention, votre version de Logisim
  //   ne contient pas de tracker. Si vous
  //   enregistrez votre projet, toutes les
  //   informations du tracker seront
  //   définitivement effacées.
endmodule

module FSM2 (
  input  CPT3,
  input  CPT7,
  input  SEND,
  input  Reset,
  output Q0_out,
  output [1:0] SR,
  output [1:0] CPT3_C,
  output [1:0] CPT7_C,
  output LED
);

  wire and_1_out, and_2_out, and_3_out, and_4_out, and_5_out, and_6_out, and_7_out, and_8_out, CK, not_1_out,
       not_2_out, not_3_out, not_4_out, not_5_out, not_6_out, not_7_out, not_8_out, or_1_out, or_2_out, Q1_q;

  Clock clock_1 (.out(CK));
  not not_1 (not_1_out, CPT7);
  and and_1 (and_1_out, not_1_out, CPT7_C[1]);
  not not_2 (not_2_out, CPT3);
  and and_2 (and_2_out, not_2_out, CPT3_C[1]);
  not not_3 (not_3_out, CPT7_C[1]);
  not not_4 (not_4_out, CPT3_C[1]);
  and and_3 (and_3_out, CPT7_C[1], CPT7);
  not not_5 (not_5_out, SEND);
  and and_4 (and_4_out, not_5_out, not_4_out, not_3_out, not_6_out);
  D_Flip_Flop Q0 (.D(or_1_out), .clk(CK), .Q(Q0_out), .reset(Reset));  // open: Qn, preset
  or or_1 (or_1_out, and_3_out, and_4_out);
  not not_6 (not_6_out, Q1_q);
  D_Flip_Flop Q1 (.D(and_5_out), .clk(CK), .Q(Q1_q), .reset(Reset));  // open: Qn, preset
  and and_5 (and_5_out, Q0_out, SEND);
  D_Flip_Flop Q2 (.D(or_2_out), .clk(CK), .Q(CPT3_C[1]), .reset(Reset));  // open: Qn, preset
  or or_2 (or_2_out, Q1_q, and_1_out, and_2_out);
  D_Flip_Flop Q3 (.D(and_6_out), .clk(CK), .Q(CPT7_C[1]), .reset(Reset));  // open: Qn, preset
  and and_6 (and_6_out, CPT3_C[1], CPT3);
  not not_7 (not_7_out, CPT7_C[1]);
  not not_8 (not_8_out, CPT7_C[1]);
  and and_7 (and_7_out, Q1_q, not_7_out);
  and and_8 (and_8_out, Reset, not_8_out);
  or or_3 (SR[0], and_7_out, CPT7_C[1]);
  not not_9 (CPT3_C[0], CPT3_C[1]);
  or or_4 (CPT7_C[0], Q0_out, and_8_out);
  and and_9 (LED, CPT7, CPT7_C[1]);

  assign SR[1] = CPT7_C[1];

  // Other names for the same wires on the sheet: Q3 = CPT7_C[1]

  // Notes on the sheet:
  //   Attention, votre version de Logisim
  //   ne contient pas de tracker. Si vous
  //   enregistrez votre projet, toutes les
  //   informations du tracker seront
  //   définitivement effacées.
endmodule

module UART2 (
  input  SEND,
  input  RST,
  input  [7:0] ENTRY,
  output [1:0] CPT3_VAL,
  output [1:0] SENDOUT,
  output [2:0] CPT7_VAL,
  output LED,
  output BIN_OUT,
  output [7:0] SHIFT_OUT
);

  wire and_1_out, and_2_out, compteur07_1_done7, cpt3_1_p3, fsm2_1_q0_out, not_1_out, not_2_out,
       shiftregistre8bits_1_bit_out;
  wire [1:0] fsm2_1_cpt3_c, fsm2_1_cpt7_c;

  Clock sysclk ();  // open: out
  FSM2 fsm2_1 (
    .CPT3(cpt3_1_p3), .CPT7(compteur07_1_done7), .SEND(SEND), .Reset(RST), .Q0_out(fsm2_1_q0_out),
    .SR(SENDOUT), .CPT3_C(fsm2_1_cpt3_c), .CPT7_C(fsm2_1_cpt7_c), .LED(LED));
  not not_1 (not_1_out, SENDOUT[1]);
  // CPT3 cpt3_1: pin names not known; wires that end beside it: fsm2_1_cpt3_c[1], CPT3_VAL, cpt3_1_p3
  ShiftRegistre8bits shiftregistre8bits_1 (
    .S(SENDOUT), .L(1'b0), .R(1'b0), .Inflow(ENTRY), .BIT_OUT(shiftregistre8bits_1_bit_out),
    .Outflow(SHIFT_OUT));
  Compteur07 compteur07_1 (.en(fsm2_1_cpt7_c[1]), .Reset(fsm2_1_cpt7_c[0]), .Q(CPT7_VAL), .Done7(compteur07_1_done7));
  not not_2 (not_2_out, and_1_out);
  and and_1 (and_1_out, SENDOUT[0], not_1_out);
  and and_2 (and_2_out, fsm2_1_q0_out, not_2_out);
  or or_1 (BIN_OUT, and_2_out, shiftregistre8bits_1_bit_out);

  // Notes on the sheet:
  //   Attention, votre version de Logisim
  //   ne contient pas de tracker. Si vous
  //   enregistrez votre projet, toutes les
  //   informations du tracker seront
  //   définitivement effacées.
endmodule

module screens (
);

  ShiftRegistre8bits shiftregistre8bits_1 ();  // open: S, L, R, Inflow, BIT_OUT, Outflow

  // Notes on the sheet:
  //   Attention, votre version de Logisim
  //   ne contient pas de tracker. Si vous
  //   enregistrez votre projet, toutes les
  //   informations du tracker seront
  //   définitivement effacées.
endmodule
